# Fritzing sketch 70cm-LPF_dl7bst (saved by Fritzing 0.9.2b)
circuit board: 3cm x 3cm
breadboards: 1

parts:
  1nF = Ceramic Capacitor [capacitance=1nF package="100 mil [THT, multilayer]"]
  680Ω = Resistor [tolerance=±5% resistance=680 package=THT]
  2-10pF = Variable Capacitor [capacitance=100nF max_capacitance=10pF min_capacitance=2.1pF voltage=35V]
  22pF = Ceramic Capacitor [capacitance=22pF package="100 mil [THT, multilayer]"]
  ANT = Antenna
  J1 = double row female pin header, 20 pins [form="♀ (female)"]
  22nH = Inductor [inductance=22nH package="1206 [SMD]"]

nets:
  N1: 1nF.0, 2-10pF.1, 22nH.pin_0
  N2: 1nF.1, 680Ω.Pin_1
  N3: 680Ω.Pin_0, J1.pin16
  GND: 2-10pF.0, 22pF.0, J1.pin17
  N4: 22pF.1, ANT.antenna_lead, 22nH.pin_1

notes:
  RPiTX LPF 70cm
