# Fritzing sketch Kurzwellendetektor (saved by Fritzing 0.9.3b)
breadboards: 1

parts:
  L1 = Inductor [part_number="25 Windugen" package="400 mil [THT]"]
  C1 = CAP_ADJ [part_number=256pF package=ctz3]
  D1 = Diode [package=diode-1n4001]
  ANT1 = Antenna [part_number=Antenne]
  SPKR1 = Loudspeaker

nets:
  N1: L1.pin_0, C1.3, D1.A, ANT1.antenna_lead
  GND: L1.pin_1, C1.4, SPKR1.pin2
  N2: D1.C, SPKR1.pin1
